# Fritzing sketch Levelsensor (saved by Fritzing 0.9.6b)
perfboards: 1

parts:
  J1 = JST-03JQ-BT [part_number=JST-JQ-BT package=THT]
  J2 = JST-03JQ-BT [part_number=JST-JQ-BT package=THT]
  J3 = Camdenboss CTB0158-2 [part_number=CTB0158-2 package=THT]
  R1 = Resistor [tolerance=±5% resistance=2.2k package=THT]
  R2 = Resistor [tolerance=±5% resistance=2.2k package=THT]
  R3 = Resistor [tolerance=±5% resistance=10k package=THT]
  U1 = Sharp PC817 [package=THT]

nets:
  N1: J1.pin2, J3.pin2, U1.Pin_2
  N2: J1.pin1, J3.pin1
  N3: J1.pin3, R1.Pin_0, R2.Pin_0
  N4: J2.pin2, R3.Pin_1
  N5: J2.pin1, U1.Pin_4
  N6: J2.pin3, R3.Pin_0, U1.Pin_3
  N7: R1.Pin_1, R2.Pin_1, U1.Pin_1
